// Logisim project milestone1.circ as structural Verilog: 1 circuit, main circuit main
module main (
  input  WRITE,
  input  READ,
  input  PC_LD,
  input  AR_LD,
  input  AC_LD,
  input  DR_LD,
  input  TR_LD,
  input  IR_LD,
  input  AR_CLR,
  input  AR_INC,
  input  PC_CLR,
  input  PC_INC,
  input  AC_CLR,
  input  AC_INC,
  input  DR_CLR,
  input  DR_INC,
  input  TR_CLR,
  input  TR_INC,
  input  IR_CLR,
  input  IR_INC
);

  wire adder_1_cout, adder_2_cout, clock_1_out, or_1_out;
  wire [2:0] register_1_q;
  wire [3:0] counter_1_q, multiplexer_1_out_2;
  wire [6:0] AR_q, bit_extender_1_out, bit_extender_2_out, counter_2_q;
  wire [7:0] multiplexer_2_out, multiplexer_2_out_2;
  wire [15:0] AC_DR_out, AC_q, adder_1_out, adder_2_out, bit_extender_3_out, bit_extender_4_out, DR_q, IR_q,
       multiplexer_1_out, multiplier_1_out, multiplier_2_out, not_1_out, not_2_out, ram_1_data, TR_q;

  Adder #(.width(16)) adder_1 (.a(AC_q), .b(DR_q), .out(adder_1_out), .cout(adder_1_cout));  // open: cin
  assign AC_DR_out = DR_q & AC_q;  // AND_Gate AC_DR, 16 bits wide
  Adder #(.width(16)) adder_2 (
    .a({multiplexer_2_out_2, multiplexer_2_out}), .b(AC_q), .out(adder_2_out), .cout(adder_2_cout));  // open: cin
  assign not_1_out = ~AC_q;  // NOT_Gate not_1, 16 bits wide
  assign not_2_out = ~{multiplexer_2_out_2, multiplexer_2_out};  // NOT_Gate not_2, 16 bits wide
  Multiplier #(.width(16)) multiplier_1 (.a(DR_q), .b(AC_q), .out(multiplier_1_out));  // open: cin, cout
  Multiplier #(.width(16)) multiplier_2 (
    .a(AC_q), .b({multiplexer_2_out_2, multiplexer_2_out}), .out(multiplier_2_out));  // open: cin, cout
  or or_1 (or_1_out, adder_1_cout, adder_2_cout);
  D_Flip_Flop E (.D(or_1_out));  // open: clk, Q, Qn, preset, en, reset
  Counter #(.width(4), .max('hf)) counter_1 (.Q(counter_1_q));  // open: load, D, count, carry, clk, clr
  Multiplexer #(.select(4), .width(16)) multiplexer_1 (
    .in1(DR_q), .in2({multiplexer_2_out_2, multiplexer_2_out}), .in3(adder_1_out), .in4(adder_2_out),
    .in5(AC_DR_out), .in6(not_1_out), .in7(not_2_out), .in8(multiplier_1_out), .in9(multiplier_2_out),
    .out({multiplexer_1_out[15:8], multiplexer_1_out_2, multiplexer_1_out[3:0]}), .sel(counter_1_q));  // open: in0, in10, in11, in12, in13, in14, in15, en
  Bit_Extender #(.in_width(16), .out_width(7)) bit_extender_1 (
    .in({multiplexer_2_out_2, multiplexer_2_out}), .out(bit_extender_1_out));
  Bit_Extender #(.in_width(16), .out_width(7)) bit_extender_2 (
    .in({multiplexer_2_out_2, multiplexer_2_out}), .out(bit_extender_2_out));
  RAM #(.addrWidth(7), .dataWidth(16), .bus("separate")) ram_1 (
    .addr(AR_q), .din({multiplexer_2_out_2, multiplexer_2_out}), .data(ram_1_data), .str(WRITE),
    .clk(clock_1_out), .ld(READ));  // open: sel, clr
  Counter #(.width(7), .max('h7f)) AR (
    .load(AR_LD), .D(bit_extender_1_out), .count(AR_INC), .Q(AR_q), .clk(clock_1_out), .clr(AR_CLR));  // open: carry
  Counter #(.width(7), .max('h7f)) counter_2 (
    .load(PC_LD), .D(bit_extender_2_out), .count(PC_INC), .Q(counter_2_q), .carry(PC_INC), .clk(clock_1_out),
    .clr(PC_CLR));
  Counter #(.width(16), .max('hffff)) AC (
    .load(AC_LD), .D({multiplexer_1_out[15:8], multiplexer_1_out_2, multiplexer_1_out[3:0]}), .count(AC_INC),
    .Q(AC_q), .clk(clock_1_out), .clr(AC_CLR));  // open: carry
  Counter #(.width(16), .max('hffff)) DR (
    .load(DR_LD), .D({multiplexer_2_out_2, multiplexer_2_out}), .count(DR_INC), .Q(DR_q), .clk(clock_1_out),
    .clr(DR_CLR));  // open: carry
  Counter #(.width(16), .max('hffff)) TR (
    .load(TR_LD), .D({multiplexer_2_out_2, multiplexer_2_out}), .count(TR_INC), .Q(TR_q), .clk(clock_1_out),
    .clr(TR_CLR));  // open: carry
  Counter #(.width(16), .max('hffff)) IR (
    .load(IR_LD), .D({multiplexer_2_out_2, multiplexer_2_out}), .count(IR_INC), .Q(IR_q), .clk(clock_1_out),
    .clr(IR_CLR));  // open: carry
  Clock clock_1 (.out(clock_1_out));
  Hex_Digit_Display hex_digit_display_1 (.value(multiplexer_1_out[15:12]));  // open: dp
  Register #(.width(3)) register_1 (.Q(register_1_q));  // open: D, en, clk, clr
  assign bit_extender_3_out = {{9{1'b0}}, AR_q};  // Bit_Extender bit_extender_3
  assign bit_extender_4_out = {{9{1'b0}}, counter_2_q};  // Bit_Extender bit_extender_4
  Hex_Digit_Display hex_digit_display_2 (.value(multiplexer_1_out_2));  // open: dp
  Hex_Digit_Display hex_digit_display_3 (.value(multiplexer_1_out[11:8]));  // open: dp
  Hex_Digit_Display hex_digit_display_4 (.value(multiplexer_1_out[3:0]));  // open: dp
  Multiplexer #(.select(3), .width(16)) multiplexer_2 (
    .in1(bit_extender_3_out), .in2(bit_extender_4_out), .in3(AC_q), .in4(DR_q), .in5(TR_q), .in6(ram_1_data),
    .in7(IR_q), .out({multiplexer_2_out_2, multiplexer_2_out}), .sel(register_1_q));  // open: in0, en
  Hex_Digit_Display hex_digit_display_5 (.value(multiplexer_2_out_2[7:4]));  // open: dp
  Hex_Digit_Display hex_digit_display_6 (.value(multiplexer_2_out[7:4]));  // open: dp
  Hex_Digit_Display hex_digit_display_7 (.value(multiplexer_2_out_2[3:0]));  // open: dp
  Hex_Digit_Display hex_digit_display_8 (.value(multiplexer_2_out[3:0]));  // open: dp

  // Notes on the sheet:
  //   AC
  //   DR
  //   BUS
endmodule
