// Logisim project milestone2.circ as structural Verilog: 2 circuits, main circuit ALU
module main (
  input  INC_AR,
  input  CLR_AR,
  input  CLR_PC,
  input  INC_AC,
  input  CLR_AC,
  input  in_6,
  input  in_7,
  input  CLR_DR,
  input  CLR_TR,
  input  in_10,
  input  in_11,
  input  in_12,
  input  in_13
);

  wire AC_LD_out, and_11_out, AR_LD_out, CLOCK_out, D0, D1, D2, D3, D4, D5, D6, D7, d_ff_1_q, DR_LD_out,
       MR_out, Mw_out, nor_1_out, nor_2_out, or_1_out, PC_inc_out, T0, T1, T2, T3, T3D0, T3D1, T3D2, T3D3,
       T3D4, T3D5, T3D6, T4, T4D0, T4D6, T5, T5D6, T6, T7, T8, T9, T10, T11, T12, T13, T14, T15;
  wire [2:0] multiplexer_1_out_3, or_4_out, register_1_q;
  wire [3:0] _4_bit_SC_q, bit_extender_1_out, bit_extender_6_out, C0_out;
  wire [6:0] AR_q, bit_extender_2_out, bit_extender_3_out, multiplexer_1_out, PC_q;
  wire [15:0] AC_q, ALU_output, bit_extender_4_out, bit_extender_5_out, DR_q, IR_q, ram_1_data, TR_q;
  wire [15:7] multiplexer_1_out_2;

  and and_1 (T3D0, T3, D0);
  and and_2 (T4D0, T4, D0);
  and and_3 (T3D1, T3, D1);
  and and_4 (T3D2, T3, D2);
  and and_5 (T3D3, T3, D3);
  and and_6 (T3D4, T3, D4);
  and and_7 (T3D5, T3, D5);
  and and_8 (T3D6, T3, D6);
  and and_9 (T4D6, T4, D6);
  and and_10 (T5D6, T5, D6);
  Hex_Digit_Display hex_digit_display_1 (.value(bit_extender_1_out));  // open: dp
  assign bit_extender_1_out = {{1{1'b0}}, register_1_q};  // Bit_Extender bit_extender_1
  nor nor_1 (nor_1_out, T0, T1);
  Decoder #(.select(3)) decoder_1 (
    .out0(D0), .out1(D1), .out2(D2), .out3(D3), .out4(D4), .out5(D5), .out6(D6), .out7(D7),
    .sel(register_1_q), .en(nor_1_out));
  Counter #(.width(4), .max('hf)) _4_bit_SC (
    .Q(_4_bit_SC_q), .clk(CLOCK_out), .clr(d_ff_1_q));  // open: load, D, count, carry
  or or_1 (or_1_out, T3D3, T3D4, T3D2, T3D1, T4D0, T5D6, T3D5);
  Register #(.width(3)) register_1 (.D(multiplexer_1_out_3), .Q(register_1_q), .clk(T2));  // open: en, clr
  Decoder #(.select(4)) decoder_2 (
    .out0(T0), .out1(T1), .out2(T2), .out3(T3), .out4(T4), .out5(T5), .out6(T6), .out7(T7), .out8(T8),
    .out9(T9), .out10(T10), .out11(T11), .out12(T12), .out13(T13), .out14(T14), .out15(T15), .sel(_4_bit_SC_q));  // open: en
  Hex_Digit_Display hex_digit_display_2 (.value(_4_bit_SC_q));  // open: dp
  D_Flip_Flop d_ff_1 (.clk(CLOCK_out), .D(or_1_out), .Q(d_ff_1_q));  // open: Qn, preset, en, reset
  nor nor_2 (nor_2_out, multiplexer_1_out[0], multiplexer_1_out[1], multiplexer_1_out[2], multiplexer_1_out[3], multiplexer_1_out[4], multiplexer_1_out[5], multiplexer_1_out[6], multiplexer_1_out_2[7], multiplexer_1_out_2[8], multiplexer_1_out_2[9], multiplexer_1_out_2[10], multiplexer_1_out_2[11], multiplexer_1_out_3[0], multiplexer_1_out_3[1], multiplexer_1_out_3[2], multiplexer_1_out_2[15]);
  and and_11 (and_11_out, nor_2_out, T5D6);
  or MR (MR_out, T3D6, T1, T3D0, T3D1, T3D2, T3D5);
  or AR_LD (AR_LD_out, T0, T2);
  or PC_inc (PC_inc_out, T1, and_11_out);
  or AC_LD (AC_LD_out, T4D0, T3D1, T3D2, T3D5, in_6);
  or C3 (C0_out[3], T3D5, in_10);
  or C2 (C0_out[2], T4D0, T3D1, in_11);
  or C1 (C0_out[1], T3D2, in_12);
  or C0 (C0_out[0], T4D0, T3D5, in_13);
  or Mw (Mw_out, T5D6, T3D3);
  Clock CLOCK (.out(CLOCK_out));
  or DR_LD (DR_LD_out, T3D0, in_7);
  or or_2 (or_4_out[2], T1, T1, T2, T3D1, T3D0, T3D2, T3D5, T3D6, T5D6);
  or or_3 (or_4_out[1], T4D0, T3D0, T3D1, T3D2, T0, T1, T3D3, T3D5, T3D6, T5D6);
  Bit_Extender #(.in_width(16), .out_width(7)) bit_extender_2 (
    .in({multiplexer_1_out_2[15], multiplexer_1_out_3, multiplexer_1_out_2[11:7], multiplexer_1_out}),
    .out(bit_extender_2_out));
  Bit_Extender #(.in_width(16), .out_width(7)) bit_extender_3 (
    .in({multiplexer_1_out_2[15], multiplexer_1_out_3, multiplexer_1_out_2[11:7], multiplexer_1_out}),
    .out(bit_extender_3_out));
  ALU ALU (
    .DR(DR_q), .AC(AC_q),
    .BUS({multiplexer_1_out_2[15], multiplexer_1_out_3, multiplexer_1_out_2[11:7], multiplexer_1_out}),
    .OUTPUT(ALU_output), .C3C2C1C0(C0_out));
  or or_4 (or_4_out[0], T3D4, T4D0, T3D3, T5D6, T2);
  Counter #(.width(7), .max('h7f)) AR (
    .load(AR_LD_out), .D(bit_extender_2_out), .count(INC_AR), .Q(AR_q), .clk(CLOCK_out), .clr(CLR_AR));  // open: carry
  Counter #(.width(7), .max('h7f)) PC (
    .load(T3D4), .D(bit_extender_3_out), .count(PC_inc_out), .Q(PC_q), .clk(CLOCK_out), .clr(CLR_PC));  // open: carry
  Counter #(.width(16), .max('hffff)) DR (
    .load(DR_LD_out),
    .D({multiplexer_1_out_2[15], multiplexer_1_out_3, multiplexer_1_out_2[11:7], multiplexer_1_out}),
    .count(T4D6), .Q(DR_q), .clk(CLOCK_out), .clr(CLR_DR));  // open: carry
  Register #(.width(16)) IR (
    .D({multiplexer_1_out_2[15], multiplexer_1_out_3, multiplexer_1_out_2[11:7], multiplexer_1_out}),
    .en(T1), .Q(IR_q), .clk(CLOCK_out));  // open: clr
  Counter #(.width(16), .max('hffff)) TR (
    .load(T3D6),
    .D({multiplexer_1_out_2[15], multiplexer_1_out_3, multiplexer_1_out_2[11:7], multiplexer_1_out}),
    .count(T4D6), .Q(TR_q), .clk(CLOCK_out), .clr(CLR_TR));  // open: carry
  assign bit_extender_4_out = {{9{1'b0}}, AR_q};  // Bit_Extender bit_extender_4
  assign bit_extender_5_out = {{9{1'b0}}, PC_q};  // Bit_Extender bit_extender_5
  Counter #(.width(16), .max('hffff)) AC (
    .load(AC_LD_out), .D(ALU_output), .count(INC_AC), .Q(AC_q), .clk(CLOCK_out), .clr(CLR_AC));  // open: carry
  RAM #(.addrWidth(7), .dataWidth(16), .bus("separate")) ram_1 (
    .addr(AR_q),
    .din({multiplexer_1_out_2[15], multiplexer_1_out_3, multiplexer_1_out_2[11:7], multiplexer_1_out}),
    .data(ram_1_data), .str(Mw_out), .clk(CLOCK_out), .ld(MR_out));  // open: sel, clr
  Hex_Digit_Display hex_digit_display_3 (.value(bit_extender_6_out));  // open: dp
  assign bit_extender_6_out = {{1{1'b0}}, or_4_out};  // Bit_Extender bit_extender_6
  Multiplexer #(.select(3), .width(16), .enable("false")) multiplexer_1 (
    .in1(bit_extender_4_out), .in2(bit_extender_5_out), .in3(AC_q), .in4(DR_q), .in5(IR_q), .in6(ram_1_data),
    .in7(TR_q),
    .out({multiplexer_1_out_2[15], multiplexer_1_out_3, multiplexer_1_out_2[11:7], multiplexer_1_out}),
    .sel(or_4_out));  // open: in0
  Hex_Digit_Display hex_digit_display_4 (.value({multiplexer_1_out_2[15], multiplexer_1_out_3}));  // open: dp
  Hex_Digit_Display hex_digit_display_5 (.value(multiplexer_1_out_2[11:8]));  // open: dp
  Hex_Digit_Display hex_digit_display_6 (.value(multiplexer_1_out[3:0]));  // open: dp
  Hex_Digit_Display hex_digit_display_7 (.value({multiplexer_1_out_2[7], multiplexer_1_out[6:4]}));  // open: dp

  // Notes on the sheet:
  //   Opcode
  //   T
endmodule

module ALU (
  input  [15:0] DR,
  input  [15:0] AC,
  input  [15:0] BUS,
  input  [3:0] C3C2C1C0,
  output [15:0] OUTPUT
);

  wire [15:0] adder_1_out, adder_2_out, and_1_out, multiplier_1_out, multiplier_2_out, not_1_out, not_2_out;

  Adder #(.width(16)) adder_1 (.a(DR), .b(AC), .out(adder_1_out));  // open: cin, cout
  Adder #(.width(16)) adder_2 (.a(AC), .b(BUS), .out(adder_2_out));  // open: cin, cout
  assign not_1_out = ~AC;  // NOT_Gate not_1, 16 bits wide
  assign not_2_out = ~BUS;  // NOT_Gate not_2, 16 bits wide
  assign and_1_out = DR & AC;  // AND_Gate and_1, 16 bits wide
  Multiplier #(.width(16)) multiplier_1 (.a(DR), .b(AC), .out(multiplier_1_out));  // open: cin, cout
  Multiplier #(.width(16)) multiplier_2 (.a(AC), .b(BUS), .out(multiplier_2_out));  // open: cin, cout
  Multiplexer #(.select(4), .width(16)) multiplexer_1 (
    .in1(DR), .in2(BUS), .in3(adder_1_out), .in4(adder_2_out), .in5(and_1_out), .in6(not_1_out),
    .in7(not_2_out), .in8(multiplier_1_out), .in9(multiplier_2_out), .out(OUTPUT), .sel(C3C2C1C0));  // open: in0, in10, in11, in12, in13, in14, in15, en
endmodule
